# Fritzing sketch Circuit (saved by Fritzing 0.9.3b)

parts:
  esp1 = ESP32 DevKitc V4
  Part1 = LCD1602-I2C
  Part2 = RFID-RC522-v2

nets:
  N1: esp1.IO21, Part1.SDA
  N2: esp1.IO22, Part1.SCL
  N3: esp1.GND#18, Part1.GND
  3V3: esp1.3V3, Part2.3.3V
  N4: esp1.IO33, Part2.RST
  N5: esp1.IO25, Part2.MISO
  N6: esp1.IO26, Part2.MOSI
  N7: esp1.IO27, Part2.SCK
  N8: esp1.IO14, Part2.SDA
  N9: esp1.GND#32, Part2.GND
  5V: esp1.5V, Part1.VCC

custom parts:
  ESP32 DevKitc V4: ESP32-DevKitC board with ESP32-WROOM-32 module. ESP32-DevKitC V4 is a small-sized ESP32-based development board produced by Espressif. Most of the pins on the ESP module are broken out to the pin headers on the board. The pins D0, D1, D2, D3, CMD and CLK are used internally for communication between ESP32 and SPI flash memory. They are grouped on both sides near the USB connector. Avoid using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
  LCD1602-I2C: A standard character display, usually with 2x16 characters. Comes in many colors with LCM1602 IIC attached.
  RFID-RC522-v2: A simple China made RFID-RC522 Reader; do check the pin labels, as this is a MFRC522 based clone.
